# Fritzing sketch Chapelet (saved by Fritzing 0.9.3b)
breadboards: 1

parts:
  R1 = Resistor [tolerance=±5% resistance=220 package=THT]  # not connected
  LED1 = LED - 5mm [color="Red (633nm)" package="5 mm [THT]"]  # not connected
  LED2 = LED - 5mm [color="Red (633nm)" package="5 mm [THT]"]
  LED3 = LED - 5mm [color="Red (633nm)" package="5 mm [THT]"]
  LED4 = LED - 5mm [color="Red (633nm)" package="5 mm [THT]"]  # not connected
  LED5 = LED - 5mm [color="Red (633nm)" package="5 mm [THT]"]  # not connected
  LED6 = LED - 5mm [color="Red (633nm)" package="5 mm [THT]"]  # not connected
  LED7 = LED - 5mm [color="Red (633nm)" package="5 mm [THT]"]  # not connected
  LED8 = LED - 5mm [color="Red (633nm)" package="5 mm [THT]"]
  LED9 = LED - 5mm [color="Red (633nm)" package="5 mm [THT]"]
  LED10 = LED - 5mm [color="Red (633nm)" package="5 mm [THT]"]  # not connected
  U1 = 74HC595 [package="DIP16 [THT]"]

nets:
  N1: LED2.cathode, U1.Q0
  N2: LED2.anode, U1.DS
  N3: LED3.cathode, U1.ST_CP
  N4: LED3.anode, U1.SH_CP
  N5: LED8.cathode, U1.Q2
  N6: LED8.anode, U1.Q3
  N7: LED9.cathode, U1.Q6
  N8: LED9.anode, U1.Q7
