# Fritzing sketch Chapelet_arduino (saved by Fritzing 0.9.3b)
breadboards: 3

parts:
  R10 = Resistor [tolerance=±5% resistance=150 package=THT]
  LED10 = LED - 5mm [color="Red (633nm)" package="5 mm [THT]"]
  LED08 = LED - 5mm [color="Red (633nm)" package="5 mm [THT]"]
  LED07 = LED - 5mm [color="Red (633nm)" package="5 mm [THT]"]
  Shift_Register = 74HC595 [package="DIP16 [THT]"]
  LED06 = LED - 5mm [color="Red (633nm)" package="5 mm [THT]"]
  LED05 = LED - 5mm [color="Red (633nm)" package="5 mm [THT]"]
  LED04 = LED - 5mm [color="Red (633nm)" package="5 mm [THT]"]
  LED03 = LED - 5mm [color="Red (633nm)" package="5 mm [THT]"]
  LED02 = LED - 5mm [color="Red (633nm)" package="5 mm [THT]"]
  LED01 = LED - 5mm [color="Red (633nm)" package="5 mm [THT]"]
  R09 = Resistor [tolerance=±5% resistance=150 package=THT]
  R08 = Resistor [tolerance=±5% resistance=150 package=THT]
  R07 = Resistor [tolerance=±5% resistance=150 package=THT]
  R06 = Resistor [tolerance=±5% resistance=150 package=THT]
  R05 = Resistor [tolerance=±5% resistance=150 package=THT]
  R04 = Resistor [tolerance=±5% resistance=150 package=THT]
  R03 = Resistor [tolerance=±5% resistance=150 package=THT]
  R02 = Resistor [tolerance=±5% resistance=150 package=THT]
  Arduino_Uno = Arduino Uno (Rev3)
  LED09 = LED - 5mm [color="Red (633nm)" package="5 mm [THT]"]
  Vibreur = Vibration Motor- ROB-08449 [package=vibe-motor-10mm]
  Switch = Pushbutton [package=THT]
  R11 = Resistor [tolerance=±5% resistance=1k package=THT]
  R01 = Resistor [tolerance=±5% resistance=150 package=THT]

nets:
  N1: R10.Pin_0, LED10.cathode
  N2: R10.Pin_1, Arduino_Uno.D13/SCK
  GND: LED10.anode, LED08.anode, LED07.anode, Shift_Register.GND, Shift_Register.OE, LED06.anode, LED05.anode, LED04.anode, LED03.anode, LED02.anode, LED01.anode, Arduino_Uno.GND, LED09.anode, Vibreur.+, R11.Pin_0
  N3: LED08.cathode, R08.Pin_0
  N4: LED07.cathode, R07.Pin_0
  N5: Shift_Register.Q1, R02.Pin_1
  N6: Shift_Register.Q2, R03.Pin_1
  N7: Shift_Register.Q3, R04.Pin_1
  N8: Shift_Register.Q4, R05.Pin_1
  N9: Shift_Register.Q5, R06.Pin_1
  N10: Shift_Register.Q6, R07.Pin_1
  N11: Shift_Register.Q7, R08.Pin_1
  VCC: Shift_Register.MR, Shift_Register.VCC, Arduino_Uno.5V, Switch.leg1
  N12: Shift_Register.SH_CP, Arduino_Uno.D9_PWM
  N13: Shift_Register.ST_CP, Arduino_Uno.D8
  N14: Shift_Register.DS, Arduino_Uno.D7
  N15: Shift_Register.Q0, R01.Pin_1
  N16: LED06.cathode, R06.Pin_0
  N17: LED05.cathode, R05.Pin_0
  N18: LED04.cathode, R04.Pin_0
  N19: LED03.cathode, R03.Pin_0
  N20: LED02.cathode, R02.Pin_0
  N21: LED01.cathode, R01.Pin_0
  N22: R09.Pin_0, LED09.cathode
  N23: R09.Pin_1, Arduino_Uno.D12/MISO
  N24: Arduino_Uno.D2, Switch.leg0, R11.Pin_1
  N25: Arduino_Uno.D6_PWM, Vibreur.-
