# Fritzing sketch Chapelet_attiny84 (saved by Fritzing 0.9.3b)
breadboards: 3

parts:
  R1 = Resistor [tolerance=±5% resistance=220 package=THT]
  LED1 = LED - 5mm [color="Red (633nm)" package="5 mm [THT]"]
  LED2 = LED - 5mm [color="Red (633nm)" package="5 mm [THT]"]
  LED3 = LED - 5mm [color="Red (633nm)" package="5 mm [THT]"]
  LED4 = LED - 5mm [color="Red (633nm)" package="5 mm [THT]"]
  U1 = 74HC595 [package="DIP16 [THT]"]
  LED5 = LED - 5mm [color="Red (633nm)" package="5 mm [THT]"]
  LED6 = LED - 5mm [color="Red (633nm)" package="5 mm [THT]"]
  LED7 = LED - 5mm [color="Red (633nm)" package="5 mm [THT]"]
  LED8 = LED - 5mm [color="Red (633nm)" package="5 mm [THT]"]
  LED9 = LED - 5mm [color="Red (633nm)" package="5 mm [THT]"]
  LED10 = LED - 5mm [color="Red (633nm)" package="5 mm [THT]"]
  R2 = Resistor [tolerance=±5% resistance=220 package=THT]
  R3 = Resistor [tolerance=±5% resistance=220 package=THT]
  R4 = Resistor [tolerance=±5% resistance=220 package=THT]
  R5 = Resistor [tolerance=±5% resistance=220 package=THT]
  R6 = Resistor [tolerance=±5% resistance=220 package=THT]
  R7 = Resistor [tolerance=±5% resistance=220 package=THT]
  R8 = Resistor [tolerance=±5% resistance=220 package=THT]
  R9 = Resistor [tolerance=±5% resistance=220 package=THT]
  R10 = Resistor [tolerance=±5% resistance=220 package=THT]
  U2 = ATTiny84 [package=dip]
  R11 = Resistor [tolerance=±5% resistance=220 package=THT]
  U3 = Vibration Motor- ROB-08449 [package=vibe-motor-10mm]
  S2 = Pushbutton [package=THT]

nets:
  N1: R1.Pin_0, LED1.cathode
  N2: R1.Pin_1, U2.pin2
  N3: LED1.anode, LED2.anode, LED3.anode, LED4.anode, U1.GND, U1.OE, LED5.anode, LED6.anode, LED7.anode, LED8.anode, LED9.anode, LED10.anode, U2.pin14, R11.Pin_0, U3.+
  N4: LED2.cathode, R2.Pin_0
  N5: LED3.cathode, R3.Pin_0
  N6: LED4.cathode, R4.Pin_0
  N7: U1.Q1, R9.Pin_1
  N8: U1.Q2, R8.Pin_1
  N9: U1.Q3, R7.Pin_1
  N10: U1.Q4, R6.Pin_1
  N11: U1.Q5, R5.Pin_1
  N12: U1.Q6, R4.Pin_1
  N13: U1.Q7, R3.Pin_1
  N14: U1.MR, U2.pin3
  N15: U1.SH_CP, U2.pin10
  N16: U1.ST_CP, U2.pin9
  N17: U1.DS, U2.pin8
  N18: U1.Q0, R10.Pin_1
  N19: U1.VCC, U2.pin1, S2.leg1
  N20: LED5.cathode, R5.Pin_0
  N21: LED6.cathode, R6.Pin_0
  N22: LED7.cathode, R7.Pin_0
  N23: LED8.cathode, R8.Pin_0
  N24: LED9.cathode, R9.Pin_0
  N25: LED10.cathode, R10.Pin_0
  N26: R2.Pin_1, U2.pin12
  N27: U2.pin6, U3.-
  N28: U2.pin11, R11.Pin_1, S2.leg0

custom parts:
  ATTiny84: Atmel ATTiny84 processor. 8 ADC pins, 4 PWM pins. Available in either 10MHz or 20MHz. The last 2 pin numbers refer to arduino. D6 = Arduino 6, A6 = Arduino A6 example: PA6 (SDA/MOSI/OC1A/DI/AD6/PCINT6/D6/A6) NOTE: This part is diagrammed to suit the MIT HLT ATTiny84 core at https://github.com/damellis/attiny/
