# Fritzing sketch Chapelet_attiny84_PCB (saved by Fritzing 0.9.3b)
circuit board: 10cm x 6cm
breadboards: 3

parts:
  R10 = Resistor [tolerance=±5% resistance=150 package=THT]
  LED10 = LED - 5mm [color="Red (633nm)" package="5 mm [THT]"]
  LED09 = LED - 5mm [color="Red (633nm)" package="5 mm [THT]"]
  LED08 = LED - 5mm [color="Red (633nm)" package="5 mm [THT]"]
  LED07 = LED - 5mm [color="Red (633nm)" package="5 mm [THT]"]
  LED06 = LED - 5mm [color="Red (633nm)" package="5 mm [THT]"]
  LED05 = LED - 5mm [color="Red (633nm)" package="5 mm [THT]"]
  LED04 = LED - 5mm [color="Red (633nm)" package="5 mm [THT]"]
  LED03 = LED - 5mm [color="Red (633nm)" package="5 mm [THT]"]
  LED02 = LED - 5mm [color="Red (633nm)" package="5 mm [THT]"]
  LED01 = LED - 5mm [color="Red (633nm)" package="5 mm [THT]"]
  R09 = Resistor [tolerance=±5% resistance=150 package=THT]
  R08 = Resistor [tolerance=±5% resistance=150 package=THT]
  R03 = Resistor [tolerance=±5% resistance=150 package=THT]
  R02 = Resistor [tolerance=±5% resistance=150 package=THT]
  R01 = Resistor [tolerance=±5% resistance=150 package=THT]
  ATTiny84 = ATTiny84 [package=dip]
  R11 = Resistor [tolerance=±5% resistance=1k package=THT]
  Switch = Pushbutton [package=THT]
  Shift_Register = 74HC595 [package="DIP16 [THT]"]
  U1 = Vibration Motor- ROB-08449 [package=vibe-motor-10mm]
  R04 = Resistor [tolerance=±5% resistance=150 package=THT]
  R06 = Resistor [tolerance=±5% resistance=150 package=THT]
  R07 = Resistor [tolerance=±5% resistance=150 package=THT]
  R05 = Resistor [tolerance=±5% resistance=150 package=THT]
  LilyPadCoinCell = LilyPad_Coin_Cell_Battery_Holder-Switched-20mm [part_number=DEV-13883]

nets:
  N1: R10.Pin_0, LED10.cathode
  N2: R10.Pin_1, ATTiny84.pin2
  GND: LED10.anode, LED09.anode, LED08.anode, LED07.anode, LED06.anode, LED05.anode, LED04.anode, LED03.anode, LED02.anode, LED01.anode, ATTiny84.pin14, R11.Pin_0, Shift_Register.GND, U1.+, LilyPadCoinCell.GND
  N3: LED09.cathode, R09.Pin_0
  N4: LED08.cathode, R08.Pin_0
  N5: LED07.cathode, R07.Pin_0
  N6: LED06.cathode, R06.Pin_0
  N7: LED05.cathode, R05.Pin_0
  N8: LED04.cathode, R04.Pin_0
  N9: LED03.cathode, R03.Pin_0
  N10: LED02.cathode, R02.Pin_0
  N11: LED01.cathode, R01.Pin_0
  N12: R09.Pin_1, ATTiny84.pin12
  N13: R08.Pin_1, Shift_Register.Q1
  N14: R03.Pin_1, Shift_Register.Q6
  N15: R02.Pin_1, Shift_Register.Q7
  N16: R01.Pin_1, Shift_Register.Q0
  5V: ATTiny84.pin1, Switch.leg1, Shift_Register.VCC, LilyPadCoinCell.VCC
  N17: ATTiny84.pin3, Shift_Register.MR
  N18: ATTiny84.pin6, U1.-
  N19: ATTiny84.pin8, Shift_Register.DS
  N20: ATTiny84.pin9, Shift_Register.ST_CP
  N21: ATTiny84.pin10, Shift_Register.SH_CP
  N22: ATTiny84.pin11, R11.Pin_1, Switch.leg0
  N23: ATTiny84.pin13, Shift_Register.OE
  N24: Shift_Register.Q2, R07.Pin_1
  N25: Shift_Register.Q3, R06.Pin_1
  N26: Shift_Register.Q4, R05.Pin_1
  N27: Shift_Register.Q5, R04.Pin_1

notes:
  V0.1
  27/02/2018

custom parts:
  ATTiny84: Atmel ATTiny84 processor. 8 ADC pins, 4 PWM pins. Available in either 10MHz or 20MHz. The last 2 pin numbers refer to arduino. D6 = Arduino 6, A6 = Arduino A6 example: PA6 (SDA/MOSI/OC1A/DI/AD6/PCINT6/D6/A6) NOTE: This part is diagrammed to suit the MIT HLT ATTiny84 core at https://github.com/damellis/attiny/
  LilyPad_Coin_Cell_Battery_Holder-Switched-20mm: This LilyPad Coin Cell Battery Holder has a small slide switch installed on the board, in-line with the power so you can shut off your project and save batteries. This slide switch is the same as on the LilyPad Slide Switch Board, so it’s not easy to accidentally turn off or on. Just like the original Coin Cell Battery Holder, this simple board holds a 20mm coin cell battery (such as a CR2032)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

// code stored in the sketch: chapelet-numerique.ino
#define _TINY_ 1
//#define _ARDUINO_ 1

#if defined(_TINY_)
  int SER_Pin = 5;   //pin 14 on the 75HC595
  int RCLK_Pin = 4;  //pin 12 on the 75HC595
  int SRCLK_Pin = 3; //pin 11 on the 75HC595
  int DISPLAY_LEDS = 9; //pin 9 on the 75HC595
  int LED2 = 10; //pin 1
  int LED1 = 1; //pin 10
  const int buttonPin = 2; 
  const int vibreur = 7; 
  const int delay_press = 2000;
  const int delay_vibrate_short = 1000;
  const int delay_vibrate_end = 4000;

#elif defined(_ARDUINO_)
  int SER_Pin = 7;   //pin 14 on the 75HC595
  int RCLK_Pin = 8;  //pin 12 on the 75HC595
  int SRCLK_Pin = 9; //pin 11 on the 75HC595
  int LED1 = 12; //pin 12
  int LED2 = 13; //pin 13
  const int buttonPin = 2; 
  const int vibreur = 6; 
  const int delay_press = 200;
  const int delay_vibrate_short = 100;
  const int delay_vibrate_end = 1000;
#endif

int buttonState = 0;
int state = 0;
//How many of the shift registers - change this
#define number_of_74hc595s 1 
 
//do not touch
#define numOfRegisterPins number_of_74hc595s * 8
 

boolean registers[numOfRegisterPins];
 
void setup(){
#if defined(_ARDUINO_)
  Serial.begin(9600);
#endif
  pinMode(SER_Pin, OUTPUT);
  pinMode(RCLK_Pin, OUTPUT);
  pinMode(SRCLK_Pin, OUTPUT);
  pinMode(LED1, OUTPUT);
  pinMode(LED2, OUTPUT);
  pinMode(DISPLAY_LEDS, OUTPUT);
  pinMode(vibreur, OUTPUT);
  pinMode(buttonPin, INPUT);
 
  //reset all register pins
  clearRegisters();
 // writeRegisters();

 
  digitalWrite(RCLK_Pin, LOW);
 setRegisterPin(0, LOW);
  setRegisterPin(1, LOW);
  setRegisterPin(2, LOW);
  setRegisterPin(3, LOW);
  setRegisterPin(4, LOW);
  setRegisterPin(5, LOW);
 setRegisterPin(6, LOW);
 setRegisterPin(7, LOW);
  digitalWrite(RCLK_Pin, HIGH);
  digitalWrite(RCLK_Pin, LOW);
  digitalWrite(DISPLAY_LEDS, HIGH);
}               
 
//set all register pins to LOW
void clearRegisters(){
  for(int i = numOfRegisterPins - 1; i >=  0; i--){
  digitalWrite(RCLK_Pin, LOW);
     registers[i] = LOW;
  setRegisterPin(i, LOW);
  digitalWrite(RCLK_Pin, HIGH);
  digitalWrite(RCLK_Pin, LOW);
  }
} 
 
//Set and display registers
//Only call AFTER all values are set how you would like (slow otherwise)
void writeRegisters(int mode){
   digitalWrite(RCLK_Pin, LOW);
    digitalWrite(SRCLK_Pin, LOW);
    digitalWrite(SER_Pin, mode);
    digitalWrite(SRCLK_Pin, HIGH);
  digitalWrite(RCLK_Pin, HIGH);
 
}
 
//set an individual pin HIGH or LOW
void setRegisterPin(int index, int value){
  registers[index] = value;
    digitalWrite(SRCLK_Pin, LOW);
    digitalWrite(SER_Pin, value);
    digitalWrite(SRCLK_Pin, HIGH);
}

void setActivePin(int value){
  digitalWrite(RCLK_Pin, LOW);
  digitalWrite(RCLK_Pin, HIGH);
  for(int i = numOfRegisterPins - 1; i >=  0; i--){
    digitalWrite(SRCLK_Pin, LOW);
    if(i == value) {
      digitalWrite(SER_Pin, HIGH);
    }
    else digitalWrite(SER_Pin, LOW);
    digitalWrite(SRCLK_Pin, HIGH);
  }
  digitalWrite(RCLK_Pin, LOW);
}
 
 
void loop(){
 
  // read the state of the pushbutton value:
  buttonState = digitalRead(buttonPin);
 
  // check if the pushbutton is pressed.
  // if it is, the buttonState is HIGH:
  if (buttonState == HIGH) {

#if defined(_ARDUINO_)
    Serial.print("Boutton !!!!");
#endif
    next();
  }
}

void next() {
    vibrate(delay_vibrate_short);
  switch(state) {
    case 8: 
      writeRegisters(0);
      digitalWrite(LED1, HIGH); 
      state++; 
      break;
    case 9: 
      digitalWrite(LED1, LOW); 
      digitalWrite(LED2, HIGH); 
        vibrate(delay_vibrate_end);
        state=0;
      break;
    case 0: 
      digitalWrite(LED1, LOW); 
      digitalWrite(LED2, LOW);
      writeRegisters(1);
      state++; 
    break;
    default:
      writeRegisters(0);
      state++;   
    }
  
    digitalWrite(RCLK_Pin, LOW);

      delay(delay_press);
}
void vibrate(int t) {
    digitalWrite(vibreur, HIGH);
    delay(t);
    digitalWrite(vibreur, LOW);
}
